# Fritzing sketch MQ-3 Sketch (saved by Fritzing 0.9.3b)

parts:
  ESP32_-_Back1 = ESP32 - CAM
  Part1 = MQ-4
  J1 = Piezo Speaker
  Grove1 = Grove OLED 128x96
  S1 = Square Pushbutton
  M1 = DC Motor

nets:
  N1: ESP32_-_Back1.GPIO2, J1.pin2
  N2: ESP32_-_Back1.GPIO14, Grove1.SCL
  N3: ESP32_-_Back1.GPIO15, Grove1.SDA
  N4: ESP32_-_Back1.GPIO13, Part1.AO
  N5: ESP32_-_Back1.GPIO12, S1.leg0
  N6: ESP32_-_Back1.GND#7, J1.pin1, S1.leg1
  VCC: ESP32_-_Back1.3.3V, Part1.VCC, Grove1.VCC
  N7: ESP32_-_Back1.GPIO16, M1.pin_1
  N8: ESP32_-_Back1.GND#12, Grove1.GND, M1.pin_2
  N9: ESP32_-_Back1.GND#16, Part1.GND

custom parts:
  ESP32 - CAM: The ESP32-CAM has a very competitive small-size camera module that can operate independently as a minimum system with a footprint of only 27*40.5*4.5mm and a deep sleep current of up to 6mA.
